# Fritzing sketch Bop It (saved by Fritzing 1.0.4)
breadboards: 1

parts:
  Mod1 = Raspberry Pi Pico W
  TTP223B1 = TTP223B Capacitive Touch Sensor Module [part_number="Touch sensor"]
  Part1 = InvenSense MPU6050

nets:
  GND: Mod1.pin_3, Mod1.pin_8, Mod1.pin_13, Mod1.pin_18, Mod1.pin_23, Mod1.pin_28, Mod1.pin_33, Mod1.pin_38, Mod1.pin_42, TTP223B1.GND, Part1.GND
  N1: Mod1.pin_4, Part1.SDA
  N2: Mod1.pin_5, Part1.SCL
  N3: Mod1.pin_20, TTP223B1.SIG
  VCC: Mod1.pin_36, TTP223B1.VCC, Part1.VCC

custom parts:
  Raspberry Pi Pico W: Raspberry Pi Pico W. Based around the RP2040 microcontroller the Pico W is a low cost microcontroller device bringing Raspberry Pi quality, cost, and easy of use to the microcontroller space. The areas marked KEEPOUT in pcb silkscreen should not have traces running through them to avoid shorts on a soldered in module!
  TTP223B Capacitive Touch Sensor Module: The TTP223B capacitive touch sensor module uses the TTP223B IC. The appropriate voltage is approximately 2 to 5.5 volts.
